# Fritzing sketch Untitled Sketch 3 (saved by Fritzing 0.9.3b)

parts:
  Componente1 = Arduino Uno (Rev3)
  S1 = Pololu QTR-8 Reflectabce Sensor array [package=THT]

nets:
  N1: Componente1.A0, S1.pin12
  N2: Componente1.A1, S1.pin11
  N3: Componente1.A2, S1.pin10
  N4: Componente1.A3, S1.pin9
  N5: Componente1.A4/SDA, S1.pin8
  N6: Componente1.A5/SCL, S1.pin7
  N7: Componente1.D10_PWM/SS, S1.pin4
  N8: Componente1.D12/MISO, S1.pin13, S1.pin23
