# Fritzing sketch bluetooth (saved by Fritzing 0.9.3b)
perfboards: 1

parts:
  Componente1 = Arduino Uno (Rev3)
  BT1 = Bluetooth HC-06u [package=THT]
  R1 = Resistor [tolerance=±5% resistance=220 package=THT]
  R2 = Resistor [tolerance=±5% resistance=220 package=THT]
  R3 = Resistor [tolerance=±5% resistance=220 package=THT]
  S1 = H-Bridge with L298N
  M1 = DC Motor
  M2 = DC Motor
  S2 = Pololu QTR-8 Reflectabce Sensor array [package=THT]

nets:
  N1: Componente1.A0, S2.pin12
  N2: Componente1.A1, S2.pin11
  N3: Componente1.A2, S2.pin10
  N4: Componente1.A3, S2.pin9
  N5: Componente1.A4/SDA, S2.pin8
  N6: Componente1.A5/SCL, S2.pin7
  N7: Componente1.D8, S1.IN1
  N8: Componente1.D9_PWM, S1.ENA
  N9: Componente1.D10_PWM/SS, S2.pin4, S2.pin6
  N10: Componente1.D12/MISO, S2.pin13
  N11: Componente1.D2, R1.Pin_0
  N12: Componente1.D3_PWM, BT1.TXD
  N13: Componente1.D4, S1.IN4
  N14: Componente1.D5_PWM, S1.IN3
  N15: Componente1.D6_PWM, S1.ENB
  N16: Componente1.D7, S1.IN2
  5V: Componente1.5V, BT1.VCC
  GND: Componente1.GND, BT1.GND, R2.Pin_1
  N17: R1.Pin_1, R3.Pin_0
  N18: R2.Pin_0, R3.Pin_1
  N19: S1.M1-01, M2.pin_2
  N20: S1.M1-02, M2.pin_1
  N21: S1.M2-01, M1.pin_2
  N22: S1.M2-02, M1.pin_1

custom parts:
  Bluetooth HC-06u: Bluetooth HC-06 - face up, pins down 16.5mm x 37.5mm PCB
  H-Bridge with L298N: h-bridge
